// Logisim project 16-1 mux using 2-1.circ as structural Verilog: 1 circuit, main circuit main
module main (
  input  in_1,
  input  in_2,
  input  in_3,
  input  in_4,
  input  in_5,
  input  in_6,
  input  in_7,
  input  in_8,
  input  in_9,
  input  in_10,
  input  in_11,
  input  in_12,
  input  in_13,
  input  in_14,
  input  in_15,
  input  in_16,
  input  S0,
  input  S1,
  input  S2,
  input  S3,
  output out_21
);

  wire multiplexer_1_out, multiplexer_2_out, multiplexer_3_out, multiplexer_4_out, multiplexer_5_out,
       multiplexer_6_out, multiplexer_7_out, multiplexer_8_out, multiplexer_9_out, multiplexer_10_out,
       multiplexer_11_out, multiplexer_12_out, multiplexer_13_out, multiplexer_14_out;

  Multiplexer multiplexer_1 (.in0(in_1), .in1(in_2), .out(multiplexer_1_out), .sel(S0));  // open: en
  Multiplexer multiplexer_2 (.in0(in_3), .in1(in_4), .out(multiplexer_2_out), .sel(S0));  // open: en
  Multiplexer multiplexer_3 (.in0(in_5), .in1(in_6), .out(multiplexer_3_out), .sel(S0));  // open: en
  Multiplexer multiplexer_4 (.in0(in_7), .in1(in_8), .out(multiplexer_4_out), .sel(S0));  // open: en
  Multiplexer multiplexer_5 (.in0(in_9), .in1(in_10), .out(multiplexer_5_out), .sel(S0));  // open: en
  Multiplexer multiplexer_6 (.in0(in_11), .in1(in_12), .out(multiplexer_6_out), .sel(S0));  // open: en
  Multiplexer multiplexer_7 (.in0(in_13), .in1(in_14), .out(multiplexer_7_out), .sel(S0));  // open: en
  Multiplexer multiplexer_8 (.in0(in_15), .in1(in_16), .out(multiplexer_8_out), .sel(S0));  // open: en
  Multiplexer multiplexer_9 (
    .in0(multiplexer_1_out), .in1(multiplexer_2_out), .out(multiplexer_9_out), .sel(S1));  // open: en
  Multiplexer multiplexer_10 (
    .in0(multiplexer_3_out), .in1(multiplexer_4_out), .out(multiplexer_10_out), .sel(S1));  // open: en
  Multiplexer multiplexer_11 (
    .in0(multiplexer_5_out), .in1(multiplexer_6_out), .out(multiplexer_11_out), .sel(S1));  // open: en
  Multiplexer multiplexer_12 (
    .in0(multiplexer_7_out), .in1(multiplexer_8_out), .out(multiplexer_12_out), .sel(S1));  // open: en
  Multiplexer multiplexer_13 (
    .in0(multiplexer_9_out), .in1(multiplexer_10_out), .out(multiplexer_13_out), .sel(S2));  // open: en
  Multiplexer multiplexer_14 (
    .in0(multiplexer_11_out), .in1(multiplexer_12_out), .out(multiplexer_14_out), .sel(S2));  // open: en
  Multiplexer multiplexer_15 (.in0(multiplexer_13_out), .in1(multiplexer_14_out), .out(out_21), .sel(S3));  // open: en
endmodule
