// Logisim project 4-bit-adder.circ as structural Verilog: 1 circuit, main circuit main
module main (
  input  C0,
  input  C0_2,
  input  A0,
  input  A0_2,
  input  B0,
  input  B0_2,
  input  A1,
  input  A1_2,
  input  B1,
  input  B1_2,
  input  A2,
  input  A2_2,
  input  B2,
  input  B2_2,
  input  A3,
  input  A3_2,
  input  B3,
  input  B3_2,
  input  BINVERT,
  input  A0_3,
  input  B0_3,
  input  A1_3,
  input  B1_3,
  input  A2_3,
  input  B2_3,
  input  A3_3,
  input  B3_3,
  output S0,
  output S0_2,
  output S1,
  output S1_2,
  output S2,
  output S2_2,
  output S3,
  output S3_2,
  output COUT,
  output COUT_2,
  output S0_3,
  output S1_3,
  output S2_3,
  output S3_3,
  output COUT_3
);

  wire adder_1_cout, adder_2_cout, adder_3_cout, adder_5_cout, adder_6_cout, adder_7_cout, adder_9_cout,
       adder_10_cout, adder_11_cout, not_1_out, not_2_out, not_3_out, not_4_out, xor_1_out, xor_2_out,
       xor_3_out, xor_4_out;

  Adder #(.width(1)) adder_1 (.a(A0), .b(B0), .out(S0), .cin(C0), .cout(adder_1_cout));
  Adder #(.width(1)) adder_2 (.a(A1), .b(B1), .out(S1), .cin(adder_1_cout), .cout(adder_2_cout));
  Adder #(.width(1)) adder_3 (.a(A2), .b(B2), .out(S2), .cin(adder_2_cout), .cout(adder_3_cout));
  Adder #(.width(1)) adder_4 (.a(A3), .b(B3), .out(S3), .cin(adder_3_cout), .cout(COUT));
  xor xor_1 (xor_1_out, B0_3, BINVERT);
  xor xor_2 (xor_2_out, B1_3, BINVERT);
  xor xor_3 (xor_3_out, B2_3, BINVERT);
  xor xor_4 (xor_4_out, B3_3, BINVERT);
  not not_1 (not_1_out, B0_2);
  not not_2 (not_2_out, B1_2);
  not not_3 (not_3_out, B2_2);
  not not_4 (not_4_out, B3_2);
  Adder #(.width(1)) adder_5 (.a(A0_3), .b(xor_1_out), .out(S0_3), .cin(BINVERT), .cout(adder_5_cout));
  Adder #(.width(1)) adder_6 (.a(A1_3), .b(xor_2_out), .out(S1_3), .cin(adder_5_cout), .cout(adder_6_cout));
  Adder #(.width(1)) adder_7 (.a(A2_3), .b(xor_3_out), .out(S2_3), .cin(adder_6_cout), .cout(adder_7_cout));
  Adder #(.width(1)) adder_8 (.a(A3_3), .b(xor_4_out), .out(S3_3), .cin(adder_7_cout), .cout(COUT_3));
  Adder #(.width(1)) adder_9 (.a(A0_2), .b(not_1_out), .out(S0_2), .cin(C0_2), .cout(adder_9_cout));
  Adder #(.width(1)) adder_10 (.a(A1_2), .b(not_2_out), .out(S1_2), .cin(adder_9_cout), .cout(adder_10_cout));
  Adder #(.width(1)) adder_11 (.a(A2_2), .b(not_3_out), .out(S2_2), .cin(adder_10_cout), .cout(adder_11_cout));
  Adder #(.width(1)) adder_12 (.a(A3_2), .b(not_4_out), .out(S3_2), .cin(adder_11_cout), .cout(COUT_2));

  // Notes on the sheet:
  //   4-bit adder
  //   C1
  //   C2
  //   C3
  //   4-bit adder and subtractor
  //   C0
  //   C1
  //   C2
  //   C3
  //   4-bit subtractor
  //   C1
endmodule
