// Logisim project 7 segment display.circ as structural Verilog: 1 circuit, main circuit main
module main (
  input  b3,
  input  b2,
  input  b1,
  input  b0
);

  wire and_1_out, and_2_out, and_3_out, and_4_out, and_5_out, and_6_out, and_7_out, not_1_out, not_2_out,
       not_3_out, not_4_out, or_1_out, or_2_out, or_3_out, or_4_out, or_5_out, or_6_out, or_7_out,
       xnor_1_out, xnor_2_out, xor_1_out;

  not not_1 (not_1_out, b3);
  not not_2 (not_2_out, b1);
  not not_3 (not_3_out, b2);
  not not_4 (not_4_out, b0);
  and and_1 (and_1_out, not_4_out, not_2_out);
  and and_2 (and_2_out, b2, not_2_out);
  and and_3 (and_3_out, b2, not_4_out);
  xnor xnor_1 (xnor_1_out, b0, b2);
  xnor xnor_2 (xnor_2_out, b1, b0);
  and and_4 (and_4_out, not_3_out, not_4_out);
  and and_5 (and_5_out, not_3_out, b1);
  and and_6 (and_6_out, b2, not_2_out, b0);
  and and_7 (and_7_out, b1, not_4_out);
  xor xor_1 (xor_1_out, b2, b1);
  or or_1 (or_1_out, b3, b1, xnor_1_out);
  or or_2 (or_2_out, not_3_out, xnor_2_out);
  or or_3 (or_3_out, not_2_out, b0, b2);
  or or_4 (or_4_out, and_4_out, b3, and_5_out, and_6_out, and_7_out);
  or or_5 (or_5_out, and_4_out, and_7_out);
  or or_6 (or_6_out, and_1_out, b3, and_2_out, and_3_out);
  or or_7 (or_7_out, and_3_out, xor_1_out, b3);
  _7_Segment_Display u_7_segment_display_1 (
    .g(or_7_out), .f(or_6_out), .a(or_1_out), .b(or_2_out), .e(or_5_out), .d(or_4_out), .c(or_3_out));  // open: dp

  // Notes on the sheet:
  //   a
  //   b
  //   c
  //   d
  //   e
  //   f
  //   g
endmodule
