// Logisim project full-adder.circ as structural Verilog: 1 circuit, main circuit nor gate
module nor_gate (
  input  A,
  input  B,
  input  Cin,
  output Sum,
  output Cout
);

  wire And_2_out, And_out, Xor_out;

  xor Xor (Xor_out, A, B);
  and And (And_out, Cin, Xor_out);
  and And_2 (And_2_out, A, B);
  xor Xor_2 (Sum, Xor_out, Cin);
  or Or (Cout, And_out, And_2_out);
endmodule
