// Logisim project half-adder.circ as structural Verilog: 1 circuit, main circuit nor gate
module nor_gate (
  input  A,
  input  B,
  output SUM,
  output CARRY
);

  wire nand_1_out, nand_2_out, nand_3_out;

  nand nand_1 (nand_1_out, A, B);
  nand nand_2 (nand_2_out, A, nand_1_out);
  nand nand_3 (nand_3_out, nand_1_out, B);
  nand nand_4 (CARRY, nand_1_out, nand_1_out);
  nand nand_5 (SUM, nand_2_out, nand_3_out);
endmodule
