// Logisim project mod10 sync.circ as structural Verilog: 1 circuit, main circuit main
module main (
  input  in_1,
  input  Clock,
  output out_3,
  output out_4,
  output out_5,
  output out_6
);

  wire and_1_out, and_2_out, and_3_out, j_k_ff_4_qn;

  J_K_Flip_Flop j_k_ff_1 (.J(in_1), .clk(Clock), .K(in_1), .Q(out_5));  // open: Qn, preset, en, reset
  and and_1 (and_1_out, j_k_ff_4_qn, out_5);
  J_K_Flip_Flop j_k_ff_2 (.J(and_1_out), .clk(Clock), .K(out_5), .Q(out_4));  // open: Qn, preset, en, reset
  and and_2 (and_2_out, out_5, out_4, out_4);
  J_K_Flip_Flop j_k_ff_3 (.J(and_2_out), .clk(Clock), .K(and_2_out), .Q(out_3));  // open: Qn, preset, en, reset
  and and_3 (and_3_out, out_4, out_5, out_3, out_3);
  J_K_Flip_Flop j_k_ff_4 (
    .J(and_3_out), .clk(Clock), .K(out_5), .Q(out_6), .Qn(j_k_ff_4_qn));  // open: preset, en, reset
endmodule
