// Logisim project mod8-counter.circ as structural Verilog: 1 circuit, main circuit main
module main (
  input  in_1,
  input  in_2,
  output out_3,
  output out_4,
  output out_5
);

  wire and_1_out;

  J_K_Flip_Flop j_k_ff_1 (.J(in_1), .clk(in_2), .K(in_1), .Q(out_3));  // open: Qn, preset, en, reset
  J_K_Flip_Flop j_k_ff_2 (.J(out_3), .clk(in_2), .K(out_3), .Q(out_4));  // open: Qn, preset, en, reset
  and and_1 (and_1_out, out_3, out_4);
  J_K_Flip_Flop j_k_ff_3 (.J(and_1_out), .clk(in_2), .K(and_1_out), .Q(out_5));  // open: Qn, preset, en, reset
endmodule
