// Logisim project mod8-ripple-counter.circ as structural Verilog: 1 circuit, main circuit main
module main (
  input  in_1,
  input  clock,
  input  in_3,
  output Qb,
  output Qc,
  output Qa
);

  J_K_Flip_Flop j_k_ff_1 (.J(in_1), .clk(clock), .K(in_3), .Q(Qa));  // open: Qn, preset, en, reset
  J_K_Flip_Flop j_k_ff_2 (.J(in_1), .clk(Qa), .K(in_3), .Q(Qb));  // open: Qn, preset, en, reset
  J_K_Flip_Flop j_k_ff_3 (.J(in_1), .clk(Qb), .K(in_3), .Q(Qc));  // open: Qn, preset, en, reset
endmodule
