// Logisim project nor.circ as structural Verilog: 1 circuit, main circuit nor gate
module nor_gate (
  input  a,
  input  b,
  output x
);

  wire not_1_out, not_2_out;

  not not_1 (not_1_out, a);
  not not_2 (not_2_out, b);
  and and_1 (x, not_1_out, not_2_out);
endmodule
